# Fritzing sketch sketch (saved by Fritzing 0.9.2b)
breadboards: 1

parts:
  Composant1 = Arduino Uno (Rev3)
  U1 = ADXL345 [package=lga14]

nets:
  GND: Composant1.GND, U1.GND
  N1: Composant1.A4/SDA, U1.SDA
  N2: Composant1.A5/SCL, U1.SCL
  5V: Composant1.5V, U1.VDD
